// Logisim project Basic Computer.circ as structural Verilog: 19 circuits, main circuit Project
module ALU (
  input  [15:0] A,
  input  [15:0] B,
  input  [2:0] S,
  output E,
  output [15:0] O
);

  wire adder_1_cout, adder_2_cout, d_ff_1_q, subtractor_1_bout;
  wire [15:0] adder_1_out, adder_2_out, and_1_out, or_1_out, register_1_q, subtractor_1_out, xor_1_out;

  Adder #(.width(16)) adder_1 (.a(A), .b(B), .out(adder_1_out), .cout(adder_1_cout));  // open: cin
  Subtractor #(.width(16)) subtractor_1 (.a(A), .b(B), .out(subtractor_1_out), .bout(subtractor_1_bout));  // open: bin
  assign and_1_out = B & A;  // AND_Gate and_1, 16 bits wide
  assign or_1_out = A | B;  // OR_Gate or_1, 16 bits wide
  Adder #(.width(16)) adder_2 (.a(A), .b(16'h1), .out(adder_2_out), .cout(adder_2_cout));  // open: cin
  assign xor_1_out = B ^ A;  // XOR_Gate xor_1, 16 bits wide
  Multiplexer #(.select(3), .enable("false")) multiplexer_1 (
    .in0(d_ff_1_q), .in1(adder_1_cout), .in2(subtractor_1_bout), .in3(d_ff_1_q), .in4(d_ff_1_q),
    .in5(d_ff_1_q), .in6(d_ff_1_q), .in7(adder_2_cout), .out(E), .sel(S));
  Multiplexer #(.select(3), .width(16), .enable("false")) multiplexer_2 (
    .in0(register_1_q), .in1(adder_1_out), .in2(subtractor_1_out), .in3(A), .in4(and_1_out), .in5(or_1_out),
    .in6(xor_1_out), .in7(adder_2_out), .out(O), .sel(S));
  D_Flip_Flop d_ff_1 (.clk(1'b1), .D(E), .Q(d_ff_1_q), .preset(1'b0), .en(1'b1), .reset(1'b0));  // open: Qn
  Register #(.width(16)) register_1 (.D(O), .en(1'b1), .Q(register_1_q), .clk(1'b1), .clr(1'b0));
endmodule

module AR (
  input  [11:0] Data_In,
  input  LD,
  input  INR,
  input  CLR,
  input  Clk,
  output [11:0] Data_Out
);

  wire d_ff_1_q, or_1_out, xor_1_out;
  wire [11:0] adder_1_out, multiplexer_1_out;

  xor xor_1 (xor_1_out, LD, INR);
  Multiplexer #(.width(12), .enable("false")) multiplexer_1 (
    .in0(Data_In), .in1(adder_1_out), .out(multiplexer_1_out), .sel(INR));
  or or_1 (or_1_out, xor_1_out, LD);
  Register #(.width(12)) register_1 (.D(multiplexer_1_out), .en(or_1_out), .Q(Data_Out), .clk(Clk), .clr(d_ff_1_q));
  Adder #(.width(12)) adder_1 (.a(Data_Out), .b(12'h1), .out(adder_1_out));  // open: cin, cout
  D_Flip_Flop d_ff_1 (.clk(Clk), .D(CLR), .Q(d_ff_1_q));  // open: Qn, preset, en, reset
endmodule

module TR (
  input  [15:0] Data_In,
  input  LD,
  input  INR,
  input  CLR,
  input  Clk,
  output [15:0] Data_Out
);

  wire d_ff_1_q, or_1_out, xor_1_out;
  wire [15:0] adder_1_out, multiplexer_1_out;

  xor xor_1 (xor_1_out, LD, INR);
  Multiplexer #(.width(16), .enable("false")) multiplexer_1 (
    .in0(Data_In), .in1(adder_1_out), .out(multiplexer_1_out), .sel(INR));
  or or_1 (or_1_out, xor_1_out, LD);
  Register #(.width(16)) register_1 (.D(multiplexer_1_out), .en(or_1_out), .Q(Data_Out), .clk(Clk), .clr(d_ff_1_q));
  Adder #(.width(16)) adder_1 (.a(Data_Out), .b(16'h1), .out(adder_1_out));  // open: cin, cout
  D_Flip_Flop d_ff_1 (.clk(Clk), .D(CLR), .Q(d_ff_1_q));  // open: Qn, preset, en, reset
endmodule

module DR (
  input  [15:0] Data_In,
  input  LD,
  input  INR,
  input  CLR,
  input  Clk,
  output [15:0] Data_Out
);

  wire d_ff_1_q, or_1_out, xor_1_out;
  wire [15:0] adder_1_out, multiplexer_1_out;

  xor xor_1 (xor_1_out, LD, INR);
  or or_1 (or_1_out, xor_1_out, LD);
  Multiplexer #(.width(16), .enable("false")) multiplexer_1 (
    .in0(Data_In), .in1(adder_1_out), .out(multiplexer_1_out), .sel(INR));
  Register #(.width(16)) register_1 (.D(multiplexer_1_out), .en(or_1_out), .Q(Data_Out), .clk(Clk), .clr(d_ff_1_q));
  Adder #(.width(16)) adder_1 (.a(Data_Out), .b(16'h1), .out(adder_1_out));  // open: cin, cout
  D_Flip_Flop d_ff_1 (.clk(Clk), .D(CLR), .Q(d_ff_1_q));  // open: Qn, preset, en, reset
endmodule

module AC (
  input  [15:0] Data_In,
  input  LD,
  input  INR,
  input  CLR,
  input  Clk,
  output [15:0] Data_Out
);

  wire d_ff_1_q, or_1_out, xor_1_out;
  wire [15:0] adder_1_out, multiplexer_1_out;

  xor xor_1 (xor_1_out, LD, INR);
  or or_1 (or_1_out, xor_1_out, LD);
  Multiplexer #(.width(16), .enable("false")) multiplexer_1 (
    .in0(Data_In), .in1(adder_1_out), .out(multiplexer_1_out), .sel(INR));
  Register #(.width(16)) register_1 (.D(multiplexer_1_out), .en(or_1_out), .Q(Data_Out), .clk(Clk), .clr(d_ff_1_q));
  Adder #(.width(16)) adder_1 (.a(Data_Out), .b(16'h1), .out(adder_1_out));  // open: cin, cout
  D_Flip_Flop d_ff_1 (.clk(Clk), .D(CLR), .Q(d_ff_1_q));  // open: Qn, preset, en, reset
endmodule

module Project (
);

  wire alu_1_e, CLK, INR_AC, INR_PC, LD_AC, LD_AR, LD_DR, LD_IR, LD_PC, M_Enable, M_Read, M_Write;
  wire [2:0] ALU_in, Bus_in;
  wire [11:0] ARM, bit_extender_1_out, bit_extender_2_out, pc_1_data_out;
  wire [15:0] AC, alu_1_o, AR, Bus, DR, IR, M, PC, TR;

  ALU alu_1 (.A(DR), .B(AC), .S(ALU_in), .E(alu_1_e), .O(alu_1_o));
  Bit_Extender #(.in_width(16), .out_width(12)) bit_extender_1 (.in(Bus), .out(bit_extender_1_out));
  Bit_Extender #(.in_width(16), .out_width(12)) bit_extender_2 (.in(Bus), .out(bit_extender_2_out));
  D_Flip_Flop d_ff_1 (.D(alu_1_e));  // open: clk, Q, Qn, preset, en, reset
  RAM #(.addrWidth(12), .dataWidth(16), .bus("separate")) ram_1 (
    .addr(ARM), .din(Bus), .data(M), .str(M_Write), .sel(M_Enable), .clk(CLK), .ld(M_Read), .clr(1'b0));
  AR ar_1 (.Data_In(bit_extender_1_out), .LD(LD_AR), .INR(1'b0), .CLR(1'b0), .Clk(CLK), .Data_Out(ARM));
  PC pc_1 (.Data_In(bit_extender_2_out), .LD(LD_PC), .INR(INR_PC), .CLR(1'b0), .Clk(CLK), .Data_Out(pc_1_data_out));
  DR dr_1 (.Data_In(Bus), .LD(LD_DR), .INR(1'b0), .CLR(1'b0), .Clk(CLK), .Data_Out(DR));
  AC ac_1 (.Data_In(alu_1_o), .LD(LD_AC), .INR(INR_AC), .CLR(1'b0), .Clk(CLK), .Data_Out(AC));
  IR ir_1 (.Data_In(Bus), .LD(LD_IR), .INR(1'b0), .CLR(1'b0), .Clk(CLK), .Data_Out(IR));
  TR tr_1 (.Data_In(Bus), .LD(1'b0), .INR(1'b0), .CLR(1'b0), .Clk(CLK), .Data_Out(TR));
  assign AR = {{4{1'b0}}, ARM};  // Bit_Extender bit_extender_3
  assign PC = {{4{1'b0}}, pc_1_data_out};  // Bit_Extender bit_extender_4
  Clock u_Clk (.out(CLK));
  Control_Unit control_unit_1 (
    .AC(AC), .IR(IR), .CLK(CLK), .LD_AR(LD_AR), .LD_PC(LD_PC), .INR_PC(INR_PC), .LD_DR(LD_DR),
    .INR_AC(INR_AC), .LD_AC(LD_AC), .LD_IR(LD_IR), .M_Read(M_Read), .M_Write(M_Write), .M_Enable(M_Enable),
    .ALU_in(ALU_in), .BUS_in(Bus_in));
  Multiplexer #(.select(3), .width(16), .enable("false")) multiplexer_1 (
    .in0(M), .in1(AR), .in2(TR), .in3(DR), .in4(AC), .in5(PC), .in6(IR), .out(Bus), .sel(Bus_in));  // open: in7
endmodule

module IR (
  input  [15:0] Data_In,
  input  LD,
  input  INR,
  input  CLR,
  input  Clk,
  output [15:0] Data_Out
);

  wire d_ff_1_q, or_1_out, xor_1_out;
  wire [15:0] adder_1_out, multiplexer_1_out;

  xor xor_1 (xor_1_out, LD, INR);
  or or_1 (or_1_out, xor_1_out, LD);
  Multiplexer #(.width(16), .enable("false")) multiplexer_1 (
    .in0(Data_In), .in1(adder_1_out), .out(multiplexer_1_out), .sel(INR));
  Register #(.width(16)) register_1 (.D(multiplexer_1_out), .en(or_1_out), .Q(Data_Out), .clk(Clk), .clr(d_ff_1_q));
  Adder #(.width(16)) adder_1 (.a(Data_Out), .b(16'h1), .out(adder_1_out));  // open: cin, cout
  D_Flip_Flop d_ff_1 (.clk(Clk), .D(CLR), .Q(d_ff_1_q));  // open: Qn, preset, en, reset
endmodule

module PC (
  input  [11:0] Data_In,
  input  LD,
  input  INR,
  input  CLR,
  input  Clk,
  output [11:0] Data_Out
);

  wire d_ff_1_q, or_1_out, xor_1_out;
  wire [11:0] adder_1_out, multiplexer_1_out;

  xor xor_1 (xor_1_out, LD, INR);
  Multiplexer #(.width(12), .enable("false")) multiplexer_1 (
    .in0(Data_In), .in1(adder_1_out), .out(multiplexer_1_out), .sel(INR));
  or or_1 (or_1_out, xor_1_out, LD);
  Register #(.width(12)) register_1 (.D(multiplexer_1_out), .en(or_1_out), .Q(Data_Out), .clk(Clk), .clr(d_ff_1_q));
  Adder #(.width(12)) adder_1 (.a(Data_Out), .b(12'h1), .out(adder_1_out));  // open: cin, cout
  D_Flip_Flop d_ff_1 (.clk(Clk), .D(CLR), .Q(d_ff_1_q));  // open: Qn, preset, en, reset
endmodule

// CU
module Control_Unit (
  input  [15:0] AC,
  input  [15:0] IR,
  input  CLK,
  output LD_AR,
  output LD_PC,
  output INR_PC,
  output LD_DR,
  output INR_AC,
  output LD_AC,
  output LD_IR,
  output M_Read,
  output M_Write,
  output M_Enable,
  output [2:0] ALU_in,
  output [2:0] BUS_in
);

  wire CLR_SC, D0, D1, D2, D3, D4, D5, D7, I_prime, not_1_out, sync_clr_1_clr_2, T0, T1, T2, T3, T4, T5;
  wire [2:0] counter_1_q;

  not not_1 (not_1_out, CLR_SC);
  D_Flip_Flop d_ff_1 (.clk(1'b1), .D(IR[15]), .Qn(I_prime), .preset(1'b0), .en(1'b1), .reset(1'b0));  // open: Q
  Decoder #(.select(3), .enable("false")) decoder_1 (
    .out0(T0), .out1(T1), .out2(T2), .out3(T3), .out4(T4), .out5(T5), .sel(counter_1_q));  // open: out6, out7
  Counter #(.width(3), .max('h7)) counter_1 (
    .load(1'b0), .count(not_1_out), .Q(counter_1_q), .clk(CLK), .clr(sync_clr_1_clr_2));  // open: D, carry
  Sync_CLR sync_clr_1 (.CLR_2(sync_clr_1_clr_2), .Clk(CLK), .CLR(CLR_SC));
  Decoder #(.select(3), .enable("false")) decoder_2 (
    .out0(D0), .out1(D1), .out2(D2), .out3(D3), .out4(D4), .out5(D5), .out7(D7), .sel(IR[14:12]));  // open: out6
  AR_Circuit ar_circuit_1 (.T0(T0), .T2(T2), .LD(LD_AR));
  PC_Circuit pc_circuit_1 (
    .T1(T1), .T3(T3), .T4(T4), .I_prime(I_prime), .B2(IR[2]), .D4(D4), .D7(D7), .AC(AC), .LD(LD_PC),
    .INR(INR_PC));
  DR_Circuit dr_circuit_1 (.T4(T4), .D0(D0), .D1(D1), .D2(D2), .D5(D5), .LD(LD_DR));
  AC_Circuit ac_circuit_1 (
    .T3(T3), .T5(T5), .I_prime(I_prime), .B5(IR[5]), .D0(D0), .D1(D1), .D2(D2), .D5(D5), .D7(D7),
    .INR(INR_AC), .LD(LD_AC));
  IR_Circuit ir_circuit_1 (.T1(T1), .LD(LD_IR));
  Memory_Circuit memory_circuit_1 (
    .T1(T1), .T4(T4), .D0(D0), .D1(D1), .D2(D2), .D3(D3), .D5(D5), .Read(M_Read), .Write(M_Write),
    .Enable(M_Enable));
  SC_Circuit sc_circuit_1 (
    .B2(IR[2]), .B5(IR[5]), .I_prime(I_prime), .T3(T3), .T4(T4), .T5(T5), .D0(D0), .D1(D1), .D2(D2), .D3(D3),
    .D4(D4), .D5(D5), .D7(D7), .CLR(CLR_SC));
  ALU_Circuit alu_circuit_1 (.T5(T5), .D0(D0), .D1(D1), .D2(D2), .D5(D5), .ALU_in(ALU_in));
  Bus_Circuit bus_circuit_1 (
    .T0(T0), .T1(T1), .T2(T2), .T4(T4), .D0(D0), .D1(D1), .D2(D2), .D3(D3), .D4(D4), .D5(D5), .BUS_in(BUS_in));

  // Other names for the same wires on the sheet: B2 = IR[2]; B5 = IR[5]
endmodule

// ARC
module AR_Circuit (
  input  T0,
  input  T2,
  output LD
);

  or or_1 (LD, T0, T2);
endmodule

// PCC
module PC_Circuit (
  input  T1,
  input  T3,
  input  T4,
  input  I_prime,
  input  B2,
  input  D4,
  input  D7,
  input  [15:0] AC,
  output LD,
  output INR
);

  wire and_1_out, and_3_out, nor_1_out;

  and and_1 (and_1_out, T3, I_prime, B2, D7);
  nor nor_1 (nor_1_out, AC[0], AC[1], AC[2], AC[3], AC[4], AC[5], AC[6], AC[7], AC[8], AC[9], AC[10], AC[11], AC[12], AC[13], AC[14], AC[15]);
  and and_2 (LD, T4, D4);
  and and_3 (and_3_out, and_1_out, nor_1_out);
  or or_1 (INR, T1, and_3_out);
endmodule

// DRC
module DR_Circuit (
  input  T4,
  input  D0,
  input  D1,
  input  D2,
  input  D5,
  output LD
);

  wire or_1_out;

  or or_1 (or_1_out, D0, D1, D2, D5);
  and and_1 (LD, T4, or_1_out);
endmodule

// ACC
module AC_Circuit (
  input  T3,
  input  T5,
  input  I_prime,
  input  B5,
  input  D0,
  input  D1,
  input  D2,
  input  D5,
  input  D7,
  output INR,
  output LD
);

  wire or_1_out;

  and and_1 (INR, T3, I_prime, B5, D7);
  or or_1 (or_1_out, D0, D1, D2, D5);
  and and_2 (LD, T5, or_1_out);
endmodule

// IRC
module IR_Circuit (
  input  T1,
  output LD
);


  assign LD = T1;
endmodule

// MC
module Memory_Circuit (
  input  T1,
  input  T4,
  input  D0,
  input  D1,
  input  D2,
  input  D3,
  input  D5,
  output Read,
  output Write,
  output Enable
);

  wire and_1_out, or_1_out;

  or or_1 (or_1_out, D0, D1, D2, D5);
  and and_1 (and_1_out, T4, or_1_out);
  and and_2 (Write, T4, D3);
  or or_2 (Read, T1, and_1_out);
  or or_3 (Enable, Read, Write);
endmodule

// SCC
module SC_Circuit (
  input  B2,
  input  B5,
  input  I_prime,
  input  T3,
  input  T4,
  input  T5,
  input  D0,
  input  D1,
  input  D2,
  input  D3,
  input  D4,
  input  D5,
  input  D7,
  output CLR
);

  wire and_1_out, and_2_out, and_3_out, or_1_out, or_2_out, or_3_out;

  or or_1 (or_1_out, D3, D4);
  or or_2 (or_2_out, B2, B5);
  or or_3 (or_3_out, D0, D1, D2, D5);
  and and_1 (and_1_out, or_2_out, I_prime, T3, D7);
  and and_2 (and_2_out, T4, or_1_out);
  and and_3 (and_3_out, T5, or_3_out);
  or or_4 (CLR, and_1_out, and_2_out, and_3_out);
endmodule

// ALUC
module ALU_Circuit (
  input  T5,
  input  D0,
  input  D1,
  input  D2,
  input  D5,
  output [2:0] ALU_in
);

  wire and_1_out, and_2_out, and_3_out, and_4_out;

  and and_1 (and_1_out, D1, T5);
  and and_2 (and_2_out, D5, T5);
  and and_3 (and_3_out, D2, T5);
  and and_4 (and_4_out, D0, T5);
  Priority_Encoder priority_encoder_1 (
    .in0(1'b0), .in1(and_1_out), .in2(and_2_out), .in3(and_3_out), .in4(and_4_out), .in5(1'b0), .in6(1'b0),
    .in7(1'b0), .out(ALU_in), .en_in(1'b1));  // open: gs, en_out
endmodule

// BC
module Bus_Circuit (
  input  T0,
  input  T1,
  input  T2,
  input  T4,
  input  D0,
  input  D1,
  input  D2,
  input  D3,
  input  D4,
  input  D5,
  output [2:0] BUS_in
);

  wire and_1_out, and_2_out, and_3_out, or_1_out, or_2_out;

  or or_1 (or_1_out, D0, D1, D2, D5);
  and and_1 (and_1_out, T4, or_1_out);
  and and_2 (and_2_out, T4, D4);
  and and_3 (and_3_out, T4, D3);
  or or_2 (or_2_out, T1, and_1_out);
  Priority_Encoder priority_encoder_1 (
    .in0(or_2_out), .in1(and_2_out), .in2(1'b0), .in3(1'b0), .in4(and_3_out), .in5(T0), .in6(T2), .in7(1'b0),
    .out(BUS_in), .en_in(1'b1));  // open: gs, en_out
endmodule

// Sync
module Sync_CLR (
  input  Clk,
  input  CLR,
  output CLR_2
);

  D_Flip_Flop d_ff_1 (.clk(Clk), .D(CLR), .Q(CLR_2));  // open: Qn, preset, en, reset
endmodule
